# Fritzing sketch sound_alarm (saved by Fritzing 0.7.10b)
breadboards: 1

parts:
  U1 = LM 358 Dual Op-Amp [package="DIP8 [THT]"]
  C2 = Electrolytic Capacitor [capacitance=1µF voltage=50V package="100 mil [THT, electrolytic]"]
  R1 = Resistor [tolerance=±5% resistance=22k package=THT]  # not connected
  R2 = Resistor [tolerance=±5% resistance=12 package=THT]  # not connected
  R3 = Resistor [tolerance=±5% resistance=1k package=THT]  # not connected
  R6 = Resistor [tolerance=±5% resistance=39k package=THT]
  R7 = Resistor [tolerance=±5% resistance=100k package=THT]
  R8 = Resistor [tolerance=±5% resistance=100k package=THT]
  C3 = Electrolytic Capacitor [capacitance=22µF voltage=35V package="100 mil [THT, electrolytic]"]
  C4 = Electrolytic Capacitor [capacitance=470µF voltage=26V package="200 mil [THT, electrolytic]"]
  R9 = Resistor [tolerance=±5% resistance=240 package=THT]
  LED1 = LED - 5mm [color="Infrared (940nm)" package="5 mm [THT]"]
  Arduino1 = Arduino
  R10 = Rotary Potentiometer (Small) [maximum_resistance=100kΩ]
  LCD1 = LCD screen
  S1 = Pushbutton [package="[THT]"]
  R11 = Trimmer Potentiometer [package=THT]
  R5 = Resistor [tolerance=±5% resistance=1k package=THT]  # not connected
  MIC1 = Microphone

nets:
  N1: U1.connector0, U1.connector4
  N2: U1.connector1, R8.Pin_0
  GND: U1.connector3, R7.Pin_0, C3.-, C4.-, R9.Pin_0, Arduino1.GND, R10.leg1, LCD1.VSS, LCD1.R/W, LCD1.LED-, S1.Pin_2, MIC1.pin1
  N3: U1.connector5, R6.Pin_1
  N4: U1.connector6, C3.+, Arduino1.A0
  N5: U1.connector7, R6.Pin_0, C4.+
  N6: C2.+, MIC1.pin2
  N7: R9.Pin_1, LED1.cathode
  N8: LED1.anode, Arduino1.D3
  N9: Arduino1.D13, LCD1.RS
  5V: Arduino1.D12, Arduino1.+5V, R10.leg2, LCD1.VDD, LCD1.DB7, LCD1.LED+, R11.leg1, R11.leg2
  N10: Arduino1.D11, LCD1.DB6
  N11: Arduino1.D10, LCD1.DB5
  N12: Arduino1.D9, LCD1.DB4
  N13: Arduino1.D8, LCD1.E
  N14: Arduino1.D4, S1.Pin_4
  N15: Arduino1.A1, R10.wiper
  N16: LCD1.V0, R11.wiper
